// Logisim project GrandPa_test.circ as structural Verilog: 4 circuits, main circuit data_path
module data_path (
  input  load,
  input  clk,
  input  shift,
  input  reset,
  input  [7:0] number,
  output square_ready,
  output [15:0] result
);

  wire A_p13, A_p14, A_p15, A_p16, A_p17, A_p18, A_p19, A_p20, and_1_out;
  wire [3:0] R_q;
  wire [7:0] neg_1_res;
  wire [15:0] adder_1_out, B_p18;

  neg neg_1 (.number(number), .negate(number[7]), .res(neg_1_res));
  // Shift_Register A: pin names not known; wires that end beside it: load, shift, clk, 1'b0, neg_1_res[7], neg_1_res[6], neg_1_res[5], neg_1_res[4], neg_1_res[3], neg_1_res[2], neg_1_res[1], neg_1_res[0], A_p13, A_p14, A_p15, A_p16, A_p17, A_p18, A_p19, A_p20
  nor nor_1 (square_ready, A_p13, A_p14, A_p15, A_p16, A_p17, A_p18, A_p19, A_p20);
  and and_1 (and_1_out, shift, A_p20);
  // Shift_Register #(.length(16)) B: pin names not known; wires that end beside it: 1'b0, load, shift, clk, 1'b0, neg_1_res[0], neg_1_res[1], neg_1_res[2], neg_1_res[3], neg_1_res[4], neg_1_res[5], neg_1_res[6], neg_1_res[7], neg_1_res[7], neg_1_res[7], neg_1_res[7], neg_1_res[7], B_p18[0], B_p18[1], B_p18[2], B_p18[3], B_p18[4], B_p18[5], B_p18[6], B_p18[7], B_p18[8], B_p18[9], B_p18[10], B_p18[11]
  Register #(.width(16)) R (
    .D(adder_1_out), .en(and_1_out), .clk(clk), .Q({result[15], result[10:0], R_q}), .clr(reset));
  Adder #(.width(16)) adder_1 (.a(B_p18), .b({result[15], result[10:0], R_q}), .out(adder_1_out));  // open: cin, cout

  assign result[14:11] = {4{result[15]}};
endmodule

module neg (
  input  [7:0] number,
  input  negate,
  output [7:0] res
);

  wire [7:0] xor_8_out;

  xor xor_1 (xor_8_out[7], number[7], negate);
  xor xor_2 (xor_8_out[6], number[6], negate);
  xor xor_3 (xor_8_out[5], number[5], negate);
  xor xor_4 (xor_8_out[4], number[4], negate);
  xor xor_5 (xor_8_out[3], number[3], negate);
  xor xor_6 (xor_8_out[2], number[2], negate);
  xor xor_7 (xor_8_out[1], number[1], negate);
  xor xor_8 (xor_8_out[0], number[0], negate);
  Adder adder_1 (.a(xor_8_out), .b({8{1'b0}}), .out(res), .cin(negate));  // open: cout
endmodule

module sequencer (
  input  clk,
  input  NR,
  input  ST,
  input  square_ready,
  output RR,
  output reset,
  output RDy,
  output load,
  output shift
);

  wire and_1_out, count_up, d_ff_2_q, d_ff_6_q, demultiplexer_1_out0, demultiplexer_1_out1,
       demultiplexer_2_out0, demultiplexer_2_out1, demultiplexer_3_out0, demultiplexer_3_out1,
       demultiplexer_4_out0, demultiplexer_4_out1, demultiplexer_5_out0, demultiplexer_5_out1,
       demultiplexer_6_out0, demultiplexer_6_out1, or_1_out, or_3_out, or_4_out, or_5_out, or_6_out;
  wire [3:0] counter_1_q;

  or or_1 (or_1_out, demultiplexer_1_out0, demultiplexer_6_out1);
  D_Flip_Flop d_ff_1 (.D(or_1_out), .clk(clk), .Q(RR));  // open: Qn, preset, reset
  Demultiplexer demultiplexer_1 (.out0(demultiplexer_1_out0), .out1(demultiplexer_1_out1), .in(RR), .sel(ST));
  or or_2 (reset, ST, demultiplexer_1_out1);
  or or_3 (or_3_out, reset, d_ff_2_q);
  Demultiplexer demultiplexer_2 (.out0(demultiplexer_2_out0), .out1(demultiplexer_2_out1), .in(or_3_out), .sel(ST));
  D_Flip_Flop d_ff_2 (.D(demultiplexer_2_out1), .clk(clk), .Q(d_ff_2_q));  // open: Qn, preset, reset
  or or_4 (or_4_out, demultiplexer_3_out0, demultiplexer_2_out0, count_up);
  D_Flip_Flop d_ff_3 (.D(or_4_out), .clk(clk), .Q(RDy));  // open: Qn, preset, reset
  Demultiplexer demultiplexer_3 (.out0(demultiplexer_3_out0), .out1(demultiplexer_3_out1), .in(RDy), .sel(NR));
  D_Flip_Flop d_ff_4 (.D(demultiplexer_3_out1), .clk(clk), .Q(load));  // open: Qn, preset, reset
  or or_5 (or_5_out, demultiplexer_4_out0, load);
  D_Flip_Flop d_ff_5 (.D(or_5_out), .clk(clk), .Q(shift));  // open: Qn, preset, reset
  Demultiplexer demultiplexer_4 (
    .out0(demultiplexer_4_out0), .out1(demultiplexer_4_out1), .in(shift), .sel(square_ready));
  Counter #(.max('hf), .width(4)) counter_1 (
    .clr(reset), .up(1'b1), .count(count_up), .clk(clk), .Q(counter_1_q));  // open: load, D, carry
  or or_6 (or_6_out, demultiplexer_4_out1, d_ff_6_q);
  D_Flip_Flop d_ff_6 (.D(demultiplexer_5_out1), .clk(clk), .Q(d_ff_6_q));  // open: Qn, preset, reset
  Demultiplexer demultiplexer_5 (.out0(demultiplexer_5_out0), .out1(demultiplexer_5_out1), .in(or_6_out), .sel(NR));
  and and_1 (and_1_out, counter_1_q[0], counter_1_q[1], counter_1_q[2], counter_1_q[3]);
  Demultiplexer demultiplexer_6 (
    .out0(demultiplexer_6_out0), .out1(demultiplexer_6_out1), .in(demultiplexer_5_out0), .sel(and_1_out));
  D_Flip_Flop d_ff_7 (.D(demultiplexer_6_out0), .clk(clk), .Q(count_up));  // open: Qn, preset, reset
endmodule

module main (
  input  [7:0] in_1,
  input  in_2,
  input  in_3
);

  wire clock_1_out, clock_2_out, data_path_1_square_ready, sequencer_1_load, sequencer_1_rdy,
       sequencer_1_reset, sequencer_1_rr, sequencer_1_shift;
  wire [15:0] data_path_1_result;

  Clock clock_1 (.out(clock_1_out));
  sequencer sequencer_1 (
    .clk(clock_1_out), .NR(in_2), .ST(in_3), .square_ready(data_path_1_square_ready), .RR(sequencer_1_rr),
    .reset(sequencer_1_reset), .RDy(sequencer_1_rdy), .load(sequencer_1_load), .shift(sequencer_1_shift));
  LED RDy (.in(sequencer_1_rdy));
  LED RR (.in(sequencer_1_rr));
  Clock clock_2 (.out(clock_2_out));
  data_path data_path_1 (
    .load(sequencer_1_load), .clk(clock_2_out), .shift(sequencer_1_shift), .reset(sequencer_1_reset),
    .number(in_1), .square_ready(data_path_1_square_ready), .result(data_path_1_result));
  // Probe on data_path_1_result

  // Other names for the same wires on the sheet: number[7:0] = in_1
endmodule
