// Logisim project parallel.circ as structural Verilog: 9 circuits, main circuit computing_unit
module computing_unit (
  input  clk,
  input  [7:0] number,
  input  multiply,
  input  load_C,
  input  carry_in,
  input  divide,
  input  load_B,
  input  invert,
  input  load_A,
  input  add,
  input  reset_result,
  output mult_ready,
  output [15:0] Result,
  output div_ready
);

  wire and_1_out, and_2_out, or_1_out, or_2_out, or_3_out, shift_register_1_p4, shift_register_1_p14,
       shift_register_1_p15, shift_register_1_p16, shift_register_1_p17, shift_register_1_p18,
       shift_register_1_p19, shift_register_1_p20, shift_register_2_p8, shift_register_2_p9,
       shift_register_2_p10;
  wire [7:0] controlled8inverter_1_f;
  wire [15:0] adder_1_out, from8to16_1_x16, multiplexer_1_out, undriven;

  // Shift_Register shift_register_1: pin names not known; wires that end beside it: load_B, multiply, clk, shift_register_1_p4, number[7], number[6], number[5], number[4], number[3], number[2], number[1], number[0], shift_register_1_p4, shift_register_1_p14, shift_register_1_p15, shift_register_1_p16, shift_register_1_p17, shift_register_1_p18, shift_register_1_p19, shift_register_1_p20
  // Shift_Register #(.length(3)) shift_register_2: pin names not known; wires that end beside it: load_C, divide, clk, 1'b0, 1'b0, number[2], number[1], shift_register_2_p8, shift_register_2_p9, shift_register_2_p10
  nor nor_1 (mult_ready, shift_register_1_p4, shift_register_1_p14, shift_register_1_p15, shift_register_1_p16, shift_register_1_p17, shift_register_1_p18, shift_register_1_p19, shift_register_1_p20);
  and and_1 (and_1_out, shift_register_1_p20, multiply);
  or or_1 (or_1_out, shift_register_2_p8, shift_register_2_p9, shift_register_2_p10);
  or or_2 (or_2_out, and_1_out, add);
  not not_1 (div_ready, or_1_out);
  and and_2 (and_2_out, or_1_out, divide);
  // Shift_Register #(.length(16)) shift_register_3: pin names not known; wires that end beside it: load_A, multiply, clk, 1'b0
  // Shift_Register #(.length(16)) shift_register_4: pin names not known; wires that end beside it: reset_result, or_2_out, and_2_out, clk, adder_1_out[15]
  Multiplexer #(.width(16)) multiplexer_1 (.in0(undriven), .in1(from8to16_1_x16), .out(multiplexer_1_out), .sel(add));
  or or_3 (or_3_out, carry_in, invert);
  Adder #(.width(16)) adder_1 (.a(multiplexer_1_out), .b(Result), .out(adder_1_out), .cin(or_3_out));  // open: cout
  from8to16 from8to16_1 (.x8(controlled8inverter_1_f), .x16(from8to16_1_x16));
  controlled8inverter controlled8inverter_1 (.invert(invert), .x(number), .f(controlled8inverter_1_f));
endmodule

module number_loader (
  input  clk,
  input  [7:0] number,
  input  load,
  input  [1:0] register_selector,
  output [7:0] x,
  output [7:0] y,
  output [7:0] z,
  output [7:0] t
);

  wire demultiplexer_1_out0, demultiplexer_1_out1, demultiplexer_1_out2, demultiplexer_1_out3;

  Demultiplexer #(.select(2)) demultiplexer_1 (
    .out0(demultiplexer_1_out0), .out1(demultiplexer_1_out1), .out2(demultiplexer_1_out2),
    .out3(demultiplexer_1_out3), .in(load), .sel(register_selector));
  Register register_1 (.D(number), .en(demultiplexer_1_out0), .clk(clk), .Q(x));  // open: clr
  Register register_2 (.D(number), .en(demultiplexer_1_out1), .clk(clk), .Q(y));  // open: clr
  Register register_3 (.D(number), .en(demultiplexer_1_out2), .clk(clk), .Q(z));  // open: clr
  Register register_4 (.D(number), .en(demultiplexer_1_out3), .clk(clk), .Q(t));  // open: clr
endmodule

module from8to16 (
  input  [7:0] x8,
  output [15:0] x16
);


  assign x16 = {{9{x8[7]}}, x8[6:0]};
endmodule

module controlled8inverter (
  input  invert,
  input  [7:0] x,
  output [7:0] f
);

  xor xor_1 (f[7], invert, x[7]);
  xor xor_2 (f[6], invert, x[6]);
  xor xor_3 (f[5], invert, x[5]);
  xor xor_4 (f[4], invert, x[4]);
  xor xor_5 (f[3], invert, x[3]);
  xor xor_6 (f[2], invert, x[2]);
  xor xor_7 (f[1], invert, x[1]);
  xor xor_8 (f[0], invert, x[0]);
endmodule

module data_path (
  input  clk,
  input  load_B,
  input  load_const,
  input  load_C,
  input  carry_in,
  input  load_A,
  input  [7:0] \const ,
  input  [7:0] number,
  input  divide,
  input  add,
  input  multiply,
  input  load,
  input  invert,
  input  reset_result,
  input  [1:0] register_selector,
  output mult_ready,
  output [15:0] result,
  output div_ready
);

  wire [7:0] multiplexer_1_out, multiplexer_2_out, number_loader_1_t, number_loader_1_x, number_loader_1_y,
       number_loader_1_z;

  number_loader number_loader_1 (
    .clk(clk), .number(number), .load(load), .register_selector(register_selector), .x(number_loader_1_x),
    .y(number_loader_1_y), .z(number_loader_1_z), .t(number_loader_1_t));
  Multiplexer #(.select(2), .width(8)) multiplexer_1 (
    .in0(number_loader_1_x), .in1(number_loader_1_y), .in2(number_loader_1_z), .in3(number_loader_1_t),
    .out(multiplexer_1_out), .sel(register_selector));
  Multiplexer #(.width(8)) multiplexer_2 (
    .in0(multiplexer_1_out), .in1(\const ), .out(multiplexer_2_out), .sel(load_const));
  computing_unit computing_unit_1 (
    .clk(clk), .number(multiplexer_2_out), .multiply(multiply), .load_C(load_C), .carry_in(carry_in),
    .divide(divide), .load_B(load_B), .invert(invert), .load_A(load_A), .add(add),
    .reset_result(reset_result), .mult_ready(mult_ready), .Result(result), .div_ready(div_ready));
endmodule

module sequencer (
  input  NR,
  input  ST,
  input  clk,
  input  mult_ready,
  input  div_ready,
  output load_A,
  output [1:0] register_selector,
  output [7:0] \const ,
  output load_B,
  output multiply,
  output RR,
  output load_const,
  output add,
  output load,
  output RDY,
  output reset_result,
  output carry_in,
  output invert,
  output load_C,
  output divide
);

  wire comparator_1_eq, count_up, demultiplexer_1_out0, demultiplexer_1_out1, if_statement_1_false,
       if_statement_1_true, if_statement_2_false, if_statement_2_true, if_statement_3_false,
       if_statement_3_true, if_statement_4_false, if_statement_4_true, if_statement_5_false,
       if_statement_5_true, if_statement_6_false, if_statement_6_true, if_statement_7_false,
       if_statement_7_true, load_A1, load_A2, load_B1, load_B2, mult1, mult2, or_1_out, or_8_out, or_9_out,
       or_11_out, or_12_out, or_13_out, or_14_out, RR1, RR2, wait_NR_0_q;
  wire [1:0] count;

  or or_1 (or_1_out, if_statement_1_true, if_statement_3_true);
  D_Flip_Flop d_ff_1 (.D(or_1_out), .clk(clk), .Q(RR1));  // open: Qn, preset, reset
  or or_2 (add, carry_in, invert);
  or or_3 (load_A, load_A1, load_A2);
  or or_4 (load_B, load_B1, load_B2);
  or or_5 (multiply, mult1, mult2);
  or or_6 (load_const, load_B2, carry_in, load_C);
  if_statement if_statement_1 (.condition(ST), .sgn(RR1), .False(if_statement_1_false), .True(if_statement_1_true));
  or or_7 (reset_result, if_statement_1_false, ST);
  D_Flip_Flop d_ff_2 (.D(demultiplexer_1_out1), .clk(clk), .Q(load_A1));  // open: Qn, preset, reset
  D_Flip_Flop d_ff_3 (.D(if_statement_6_false), .clk(clk), .Q(load_A2));  // open: Qn, preset, reset
  D_Flip_Flop d_ff_4 (.D(if_statement_7_false), .clk(clk), .Q(carry_in));  // open: Qn, preset, reset
  D_Flip_Flop d_ff_5 (.D(invert), .clk(clk), .Q(load_C));  // open: Qn, preset, reset
  or or_8 (or_8_out, if_statement_2_true, count_up, reset_result);
  or or_9 (or_9_out, if_statement_3_false, if_statement_4_false);
  D_Flip_Flop wait_NR_1 (.D(or_8_out), .clk(clk), .Q(RDY));  // open: Qn, preset, reset
  D_Flip_Flop d_ff_6 (.D(or_9_out), .clk(clk), .Q(RR2));  // open: Qn, preset, reset
  if_statement if_statement_2 (.condition(NR), .sgn(RDY), .False(if_statement_2_false), .True(if_statement_2_true));
  D_Flip_Flop d_ff_7 (.D(load_A1), .clk(clk), .Q(load_B1));  // open: Qn, preset, reset
  assign register_selector = load_A1 ? 2'b00 : 2'bz;  // Controlled_Buffer controlled_buffer_1
  assign register_selector = load_B1 ? 2'b01 : 2'bz;  // Controlled_Buffer controlled_buffer_2
  assign register_selector = load_A2 ? 2'b10 : 2'bz;  // Controlled_Buffer controlled_buffer_3
  assign register_selector = invert ? 2'b11 : 2'bz;  // Controlled_Buffer controlled_buffer_4
  assign register_selector = load ? count : 2'bz;  // Controlled_Buffer controlled_buffer_5
  D_Flip_Flop d_ff_8 (.D(load_A2), .clk(clk), .Q(load_B2));  // open: Qn, preset, reset
  D_Flip_Flop d_ff_9 (.D(carry_in), .clk(clk), .Q(invert));  // open: Qn, preset, reset
  or or_10 (RR, RR1, RR2);
  D_Flip_Flop load_current_register (.D(if_statement_2_false), .clk(clk), .Q(load));  // open: Qn, preset, reset
  or or_11 (or_11_out, if_statement_4_true, load_C);
  if_statement if_statement_3 (.condition(ST), .sgn(RR2), .False(if_statement_3_false), .True(if_statement_3_true));
  D_Flip_Flop d_ff_10 (.D(or_11_out), .clk(clk), .Q(divide));  // open: Qn, preset, reset
  or or_12 (or_12_out, if_statement_6_true, load_B1);
  or or_13 (or_13_out, load, wait_NR_0_q);
  D_Flip_Flop d_ff_11 (.D(or_12_out), .clk(clk), .Q(mult1));  // open: Qn, preset, reset
  or or_14 (or_14_out, if_statement_7_true, load_B2);
  D_Flip_Flop wait_NR_0 (.D(if_statement_5_false), .clk(clk), .Q(wait_NR_0_q));  // open: Qn, preset, reset
  D_Flip_Flop d_ff_12 (.D(or_14_out), .clk(clk), .Q(mult2));  // open: Qn, preset, reset
  if_statement if_statement_4 (
    .condition(div_ready), .sgn(divide), .False(if_statement_4_false), .True(if_statement_4_true));
  if_statement if_statement_5 (
    .condition(NR), .sgn(or_13_out), .False(if_statement_5_false), .True(if_statement_5_true));
  assign \const  = carry_in ? {8{1'b0}} : 8'bz;  // Controlled_Buffer controlled_buffer_6
  assign \const  = load_B2 ? 8'h5 : 8'bz;  // Controlled_Buffer controlled_buffer_7
  assign \const  = load_C ? 8'h4 : 8'bz;  // Controlled_Buffer controlled_buffer_8
  Comparator #(.width(2)) comparator_1 (.a(count), .b(2'b11), .eq(comparator_1_eq));  // open: gt, lt
  Demultiplexer demultiplexer_1 (
    .out0(demultiplexer_1_out0), .out1(demultiplexer_1_out1), .in(if_statement_5_true), .sel(comparator_1_eq));
  if_statement if_statement_6 (
    .condition(mult_ready), .sgn(mult1), .False(if_statement_6_false), .True(if_statement_6_true));
  if_statement if_statement_7 (
    .condition(mult_ready), .sgn(mult2), .False(if_statement_7_false), .True(if_statement_7_true));
  D_Flip_Flop next_register (.D(demultiplexer_1_out0), .clk(clk), .Q(count_up));  // open: Qn, preset, reset
  counter2 counter2_1 (.clk(clk), .reset(reset_result), .x(count_up), .current_value(count));

  // Other names for the same wires on the sheet: add1 = carry_in; load_c0 = carry_in; load_const0 = carry_in;
  //   load_c1 = load_B2; load_const1 = load_B2; load_c2 = load_C; load_const2 = load_C; load_counter = load;
  //   add2 = invert; load_T = invert; load_X = load_A1; load_Y = load_B1; load_Z = load_A2; reset = reset_result
endmodule

module if_statement (
  input  condition,
  input  sgn,
  output False,
  output True
);

  and and_1 (False, condition, sgn);
  and and_2 (True, sgn, ~condition);  // AND_Gate
endmodule

module main (
  input  in_1,
  input  in_2,
  input  [7:0] in_3
);

  wire add, carry_in, clock_1_out, clock_2_out, div_ready, divide, invert, load, load_A, load_B, load_C,
       load_const, mult_ready, multiply, reset_result, sequencer_1_rdy, sequencer_1_rr;
  wire [1:0] register_selector;
  wire [7:0] \const ;
  wire [15:0] data_path_1_result;

  Clock clock_1 (.out(clock_1_out));
  sequencer sequencer_1 (
    .NR(in_1), .ST(in_2), .clk(clock_1_out), .mult_ready(mult_ready), .div_ready(div_ready), .load_A(load_A),
    .register_selector(register_selector), .\const (\const ), .load_B(load_B), .multiply(multiply),
    .RR(sequencer_1_rr), .load_const(load_const), .add(add), .load(load), .RDY(sequencer_1_rdy),
    .reset_result(reset_result), .carry_in(carry_in), .invert(invert), .load_C(load_C), .divide(divide));
  LedBar #(.matrixcols(2)) ledbar_1 (.led0(sequencer_1_rr), .led1(sequencer_1_rdy));
  Clock clock_2 (.out(clock_2_out));
  data_path data_path_1 (
    .clk(clock_2_out), .load_B(load_B), .load_const(load_const), .load_C(load_C), .carry_in(carry_in),
    .load_A(load_A), .\const (\const ), .number(in_3), .divide(divide), .add(add), .multiply(multiply),
    .load(load), .invert(invert), .reset_result(reset_result), .register_selector(register_selector),
    .mult_ready(mult_ready), .result(data_path_1_result), .div_ready(div_ready));
  // Probe on data_path_1_result

  // Other names for the same wires on the sheet: NR = in_1; number[7:0] = in_3; ST = in_2
endmodule

module counter2 (
  input  clk,
  input  reset,
  input  x,
  output [1:0] current_value
);

  wire and_1_out;

  D_Flip_Flop d_ff_1 ();  // open: D, clk, Q, Qn, preset, reset
  T_Flip_Flop t_ff_1 ();  // open: T, clk, Q, Qn, reset, preset
  S_R_Flip_Flop s_r_ff_1 ();  // open: S, R, clk, Q, reset, Qn, preset
  and and_1 (and_1_out, current_value[0], x);
  J_K_Flip_Flop q1 (.J(and_1_out), .K(and_1_out), .clk(clk), .Q(current_value[1]), .reset(reset));  // open: Qn, preset
  J_K_Flip_Flop q0 (.J(x), .K(x), .clk(clk), .Q(current_value[0]), .reset(reset));  // open: Qn, preset
endmodule
